// Logisim project PreprocessorCkt.circ as structural Verilog: 1 circuit, main circuit main
module main (
  input  [31:0] in_1,
  input  [31:0] in_2,
  output [4:0] out_3,
  output [10:0] out_4,
  output [10:0] out_5,
  output [19:0] out_6,
  output [19:0] out_7,
  output [31:0] out_8,
  output [31:0] out_9,
  output out_10,
  output out_11
);

  wire adder_1_cout, or_1_out;
  wire [10:0] adder_1_out, adder_2_out, multiplexer_7_out, not_1_out, not_2_out;

  Multiplexer #(.width(11), .enable("false")) multiplexer_1 (
    .in0(in_2[10:0]), .in1(in_1[10:0]), .out(out_4), .sel(adder_1_cout));
  Adder #(.width(11)) adder_1 (.a(in_1[10:0]), .b(not_1_out), .out(adder_1_out), .cin(1'b1), .cout(adder_1_cout));
  Multiplexer #(.width(20), .enable("false")) multiplexer_2 (
    .in0(in_2[30:11]), .in1(in_1[30:11]), .out(out_6), .sel(adder_1_cout));
  Multiplexer #(.enable("false")) multiplexer_3 (.in0(in_2[31]), .in1(in_1[31]), .out(out_10), .sel(adder_1_cout));
  Multiplexer #(.width(11), .enable("false")) multiplexer_4 (
    .in0(in_1[10:0]), .in1(in_2[10:0]), .out(out_5), .sel(adder_1_cout));
  Multiplexer #(.width(20), .enable("false")) multiplexer_5 (
    .in0(in_1[30:11]), .in1(in_2[30:11]), .out(out_7), .sel(adder_1_cout));
  Multiplexer #(.enable("false")) multiplexer_6 (.in0(in_1[31]), .in1(in_2[31]), .out(out_11), .sel(adder_1_cout));
  assign not_1_out = ~in_2[10:0];  // NOT_Gate not_1, 11 bits wide
  assign not_2_out = ~adder_1_out;  // NOT_Gate not_2, 11 bits wide
  Multiplexer #(.width(11), .enable("false")) multiplexer_7 (
    .in0(adder_2_out), .in1(adder_1_out), .out(multiplexer_7_out), .sel(adder_1_cout));
  Adder #(.width(11)) adder_2 (.a({11{1'b0}}), .b(not_2_out), .out(adder_2_out), .cin(1'b1));  // open: cout
  or or_1 (or_1_out, multiplexer_7_out[10], multiplexer_7_out[9], multiplexer_7_out[8], multiplexer_7_out[7], multiplexer_7_out[6], multiplexer_7_out[5]);
  Multiplexer #(.width(5), .enable("false")) multiplexer_8 (
    .in0(multiplexer_7_out[4:0]), .in1({5{1'b1}}), .out(out_3), .sel(or_1_out));
  Shifter #(.width(32), .shift("lr")) shifter_1 (.in({1'b1, out_6, {11{1'b0}}}), .\dist (out_3), .out(out_8));

  assign out_9 = {1'b1, out_7, {11{1'b0}}};

  // Notes on the sheet:
  //   Input A
  //   Greater Exponent
  //   Greater Fraction (A as per our definition)
  //   Input B
  //   Lesser Exponent
  //   Lesser fraction (B as per our definition)
  //   Shamt
  //   frac(A) converter into 32 bits
  //   frac(B) converted into 32 bits
  //   shifted frac(B)
endmodule
