// Logisim project RoundingCkt.circ as structural Verilog: 1 circuit, main circuit main
module main (
  input  [31:0] in_1,
  input  [10:0] in_2,
  output [31:0] out_3,
  output out_4
);

  wire and_1_out, comparator_1_eq, comparator_1_gt, or_1_out;

  Comparator #(.width(11), .mode("unsigned")) comparator_1 (
    .a(in_1[10:0]), .b(in_2), .gt(comparator_1_gt), .eq(comparator_1_eq));  // open: lt
  and and_1 (and_1_out, in_1[11], comparator_1_eq);
  or or_1 (or_1_out, and_1_out, comparator_1_gt);
  Adder #(.width(21)) adder_1 (.a(in_1[31:11]), .b({21{1'b0}}), .out(out_3[31:11]), .cin(or_1_out), .cout(out_4));

  assign out_3[10:0] = {11{1'b0}};

  // Notes on the sheet:
  //   Normalized 32-bit Significand
  //   1 << 10
  //   Rounded 32-bit Significand
  //   C_out (Necessary for further normalization)
endmodule
