// Logisim project SignificandAdder.circ as structural Verilog: 1 circuit, main circuit main
module main (
  input  SignA,
  input  SignB,
  input  [31:0] fracB,
  input  [31:0] fracA,
  output [31:0] Significand_to_be_Shifted,
  output Cout
);

  wire not_1_out;
  wire [31:0] adder_2_out, xor_2_out, xor_3_out;
  wire [31:31] and_1_out, xor_1_out;

  xor xor_1 (xor_1_out[31], SignA, SignB);
  Adder #(.width(32)) adder_1 (
    .a({32{1'b0}}), .b(xor_3_out), .out(Significand_to_be_Shifted), .cin(and_1_out[31]));  // open: cout
  assign xor_2_out = {32{xor_1_out[31]}} ^ fracB;  // XOR_Gate xor_2, 32 bits wide
  Adder #(.width(32)) adder_2 (.a(xor_2_out), .b(fracA), .out(adder_2_out), .cin(xor_1_out[31]), .cout(Cout));
  not not_1 (not_1_out, Cout);
  and and_1 (and_1_out[31], xor_1_out[31], not_1_out);
  assign xor_3_out = adder_2_out ^ {32{and_1_out[31]}};  // XOR_Gate xor_3, 32 bits wide
endmodule
