// Logisim project exponentNormalization.circ as structural Verilog: 1 circuit, main circuit exponent_normalization
module exponent_normalization (
  input  Cin_of_Final_Adder,
  input  [10:0] GREATER_EXPONENT,
  input  [10:0] SHAMT_FROM_FRACTION_NORMALIZATION,
  output [10:0] EXP_RESULT,
  output OVERFLOW,
  output UNDERFLOW
);

  wire adder_1_cout, not_3_out;
  wire [10:0] adder_1_out, not_1_out, not_2_out;

  assign not_1_out = ~SHAMT_FROM_FRACTION_NORMALIZATION;  // NOT_Gate not_1, 11 bits wide
  Adder #(.width(11)) adder_1 (.a(GREATER_EXPONENT), .b(not_1_out), .out(adder_1_out), .cin(1'b1), .cout(adder_1_cout));
  assign not_2_out = ~adder_1_out;  // NOT_Gate not_2, 11 bits wide
  not not_3 (not_3_out, adder_1_cout);
  Adder #(.width(11)) adder_2 (
    .a({11{1'b0}}), .b(adder_1_out), .out(EXP_RESULT), .cin(Cin_of_Final_Adder));  // open: cout
  and and_1 (OVERFLOW, EXP_RESULT[0], EXP_RESULT[1], EXP_RESULT[2], EXP_RESULT[3], EXP_RESULT[4], EXP_RESULT[5], EXP_RESULT[6], EXP_RESULT[7], EXP_RESULT[8], EXP_RESULT[9], EXP_RESULT[10]);
  or or_1 (UNDERFLOW, not_2_out[0], not_2_out[1], not_2_out[2], not_2_out[3], not_2_out[4], not_2_out[5], not_2_out[6], not_2_out[7], not_2_out[8], not_2_out[9], not_2_out[10], not_3_out);
endmodule
